# Fritzing sketch circuit diagram (saved by Fritzing 0.9.2b)
breadboards: 1

parts:
  Arduino1 = Arduino Uno (Rev3)
  U1 = TEMPERATURE-SENSOR [package=to-92]
  R1 = Resistor [tolerance=±5% resistance=10M package="2010 [SMD]"]
  Raspberry_Pi1 = Raspberry Pi B rev1  # not connected
  LED1 = LED - 5mm [color="Red (633nm)" package="5 mm [THT]"]  # not connected

nets:
  N1: Arduino1.A0, U1.VCC, R1.Pin_1
  GND: Arduino1.GND, U1.GND, U1.ADJ, R1.Pin_0

notes:
  The black 3 pinned thing is the PhotoDiode.
  The light and the photodiode are very close to each other.
