# Fritzing sketch wiring_diagram (saved by Fritzing 0.9.2b)
breadboards: 1

parts:
  Part1 = Arduino Uno (Rev3)
  R1 = Photocell (LDR) [package=THT]
  R2 = Resistor [tolerance=±5% resistance=1k package=THT]
  R3 = Rotary Potentiometer (Small) [maximum_resistance=100kΩ package=THT]  # not connected
  Part2 = Arduino Mini Proto Shield  # not connected
  R4 = Resistor [tolerance=±5% resistance=220 package=THT]
  LED1 = LED - 5mm [color="Yellow (585nm)" package="5 mm [THT]"]
  R5 = Resistor [tolerance=±5% resistance=220 package=THT]
  R6 = Resistor [tolerance=±5% resistance=10k package=THT]
  LED2 = LED - 5mm [color="Red (633nm)" package="5 mm [THT]"]
  LED3 = LED - 5mm [color="Blue (430nm)" package="5 mm [THT]"]
  U1 = EDISON  # not connected

nets:
  N1: Part1.A1, R1.pin_1, R2.Pin_0
  N2: Part1.5V, R1.pin_0
  N3: Part1.GND, R2.Pin_1, LED1.cathode, LED2.cathode, LED3.anode
  N4: R4.Pin_1, LED1.anode
  N5: R5.Pin_1, LED2.anode
  N6: R6.Pin_1, LED3.cathode

notes:
  Intel Edison attached to Sparkfun GPIO block
  Potentiometer connected to pins 25,27 and 26 on the other side
